# Fritzing sketch PiezoServo (saved by Fritzing 0.9.2b)
circuit board: 3.03975cm x 3.66426cm
breadboards: 1

parts:
  J1 = Basic Servo
  Part2 = Arduino Pro Mini v13
  Piezo_element = Piezo Speaker
  part = Resistor [tolerance=±5% resistance=1M package=THT]
  part_2 = Battery block 9V

nets:
  GND: J1.gnd, Part2.GND, Piezo_element.pin1, part.Pin_1, part_2.-
  VCC: J1.vcc, Part2.VCC
  N1: J1.pulse, Part2.D3_PWM
  N2: Part2.RAW, part_2.+
  N3: Part2.A0, Piezo_element.pin2, part.Pin_0
